# Fritzing sketch pcb (saved by Fritzing 0.9.3b)
circuit board: 30.5cm x 4.4cm
breadboards: 1

parts:
  part = Packages: [package=dil28-3]
  part_2 = Pad [width=7 height=7 connect=center]  # not connected
  part_3 = Pad [width=7 height=7 connect=center]  # not connected
  part_4 = Pad [width=7 height=7 connect=center]  # not connected
  part_5 = Pad [width=7 height=7 connect=center]  # not connected
  part_6 = Pad [width=7 height=7 connect=center]  # not connected
  part_7 = Pad [width=7 height=7 connect=center]  # not connected
  part_8 = Pad [width=7 height=7 connect=center]  # not connected
  part_9 = Pad [width=7 height=7 connect=center]  # not connected
  part_10 = Packages: [package=dil28-3]
  part_11 = Resistor [tolerance=±5% resistance=2.1k package="0603 [SMD]"]
  part_12 = Resistor [tolerance=±5% resistance=2.1k package="0603 [SMD]"]
  Pad9 = Pad [width=4.1392686666666663 height=1.9521311111111108 connect=center]  # not connected
  part_13 = Pad [width=7.902222222222222 height=5 connect=center]  # not connected
  part_14 = Pad [width=7.902222222222222 height=5 connect=center]  # not connected
  part_15 = Pad [width=7.9000000000000004 height=5 connect=center]  # not connected
  part_16 = Pad [width=5 height=5 connect=center]  # not connected
  part_17 = Pad [width=4.1392686666666663 height=1.9521311111111108 connect=center]  # not connected
  part_18 = Resistor [tolerance=±5% resistance=220 package="0603 [SMD]"]
  part_19 = Resistor [tolerance=±5% resistance=220 package="0603 [SMD]"]
  part_20 = Resistor [tolerance=±5% resistance=220 package="0603 [SMD]"]
  part_21 = Header 5x2 [package=avr_icsp]
  part_22 = Resistor [tolerance=±5% resistance=10k package="0603 [SMD]"]

nets:
  N1: part.DCPRG, part.VCC, part_22.Pin_1
  N2: part.IREF, part_11.Pin_1
  N3: part.GND, part.VPRG, part_11.Pin_0, part_18.Pin_0, part_19.Pin_0
  N4: part.BLANK, part_22.Pin_0
  N5: part_10.DCPRG, part_10.VCC, part_21.3, part_21.4
  N6: part_10.IREF, part_12.Pin_0
  N7: part_10.GND, part_10.VPRG, part_12.Pin_1, part_20.Pin_1, part_21.1, part_21.2
  N8: part_21.5, part_21.6
  N9: part_21.7, part_21.8

notes:
  o  C  D  E  +
  +
  1
  14
  15
  -
  B  A  +  F  G
  o  C  D  E
  swY
  swR
  swB
