# Fritzing sketch schematics (saved by Fritzing 0.9.3b)
circuit board: 30.5cm x 4cm
breadboards: 1

parts:
  U3 = atmega328 [package=dip]
  tenth = 7-SEGMENT-DISPLAY-1_-RED [package=7-segment-1_pth]
  one = 7-SEGMENT-DISPLAY-1_-RED [package=7-segment-1_pth]
  hundredth = 7-SEGMENT-DISPLAY-1_-RED [package=7-segment-1_pth]
  thousands = 7-SEGMENT-DISPLAY-1_-RED [package=7-segment-1_pth]
  R1 = Resistor [tolerance=±5% resistance=2.1k package=THT]
  R2 = Resistor [tolerance=±5% resistance=2.1k package=THT]
  pull_up_resistor = Resistor [tolerance=±5% resistance=10k package=THT]
  TLC_5940_top = Packages: [package=tssop28-groundpad]
  TLC_5940_bottom = Packages: [package=tssop28-groundpad]
  IC1 = DS1302 [package="SO8 [SMD]"]  # not connected
  tiny_rtc = polarizedheader 4pin 0.156in [package=THT]
  btn_mode = Pushbutton [package="[THT]"]
  btn_A = Pushbutton [package="[THT]"]
  btn_B = Pushbutton [package="[THT]"]

nets:
  N1: U3.D3_(PWM), TLC_5940_top.GSCLK, TLC_5940_bottom.GSCLK
  GND: U3.GND, R1.Pin_0, R2.Pin_0, TLC_5940_top.GND, TLC_5940_top.VPRG, TLC_5940_bottom.GND, TLC_5940_bottom.VPRG, tiny_rtc.pin1, btn_mode.Pin_3, btn_mode.Pin_4, btn_A.Pin_3, btn_A.Pin_4, btn_B.Pin_3, btn_B.Pin_4
  N2: U3.D5_(PWM), btn_B.Pin_1, btn_B.Pin_2
  N3: U3.D6_(PWM), btn_A.Pin_1, btn_A.Pin_2
  N4: U3.D7, btn_mode.Pin_1, btn_mode.Pin_2
  N5: U3.D9_(PWM), TLC_5940_top.XLAT, TLC_5940_bottom.XLAT
  N6: U3.D10_(PWM), pull_up_resistor.Pin_1, TLC_5940_top.BLANK, TLC_5940_bottom.BLANK
  N7: U3.D11_(PWM), TLC_5940_top.SIN
  N8: U3.D13, TLC_5940_top.SCLK, TLC_5940_bottom.SCLK
  N9: U3.A4, tiny_rtc.pin3
  N10: U3.A5, tiny_rtc.pin4
  N11: tenth.E, TLC_5940_bottom.OUT6
  N12: tenth.D, TLC_5940_bottom.OUT5
  12V: tenth.G1, one.G1, hundredth.G1, thousands.G1
  N13: tenth.C, TLC_5940_bottom.OUT4
  N14: tenth.DP, TLC_5940_bottom.OUT7
  N15: tenth.B, TLC_5940_top.OUT5
  N16: tenth.A, TLC_5940_top.OUT4
  N17: tenth.F, TLC_5940_top.OUT6
  N18: tenth.G, TLC_5940_top.OUT7
  N19: one.E, TLC_5940_bottom.OUT2
  N20: one.D, TLC_5940_bottom.OUT1
  N21: one.C, TLC_5940_bottom.OUT0
  N22: one.DP, TLC_5940_bottom.OUT3
  N23: one.B, TLC_5940_top.OUT1
  N24: one.A, TLC_5940_top.OUT0
  N25: one.F, TLC_5940_top.OUT2
  N26: one.G, TLC_5940_top.OUT3
  N27: hundredth.E, TLC_5940_bottom.OUT10
  N28: hundredth.D, TLC_5940_bottom.OUT9
  N29: hundredth.C, TLC_5940_bottom.OUT8
  N30: hundredth.DP, TLC_5940_bottom.OUT11
  N31: hundredth.B, TLC_5940_top.OUT9
  N32: hundredth.A, TLC_5940_top.OUT8
  N33: hundredth.F, TLC_5940_top.OUT10
  N34: hundredth.G, TLC_5940_top.OUT11
  N35: thousands.E, TLC_5940_bottom.OUT14
  N36: thousands.D, TLC_5940_bottom.OUT13
  N37: thousands.C, TLC_5940_bottom.OUT12
  N38: thousands.DP, TLC_5940_bottom.OUT15
  N39: thousands.B, TLC_5940_top.OUT13
  N40: thousands.A, TLC_5940_top.OUT12
  N41: thousands.F, TLC_5940_top.OUT14
  N42: thousands.G, TLC_5940_top.OUT15
  N43: R1.Pin_1, TLC_5940_top.IREF
  N44: R2.Pin_1, TLC_5940_bottom.IREF
  5V: pull_up_resistor.Pin_0, TLC_5940_top.DCPRG, TLC_5940_top.VCC, TLC_5940_bottom.DCPRG, TLC_5940_bottom.VCC, tiny_rtc.pin2
  N45: TLC_5940_top.SOUT, TLC_5940_bottom.SIN

notes:
  sda
